# Fritzing sketch arcade-button-led-light (saved by Fritzing 0.9.3b)
breadboards: 1

parts:
  Part1 = Arduino Uno (Rev3) - ICSP
  R1 = Resistor [tolerance=±5% resistance=10k package=THT]
  Arcade_button_switch = Toggle Switch [package=THT]
  Arcade-button_LED_(including_resistor) = LED - 5mm [color="Red (633nm)" package="5 mm [THT]"]

nets:
  N1: Part1.D2, R1.Pin_0, Arcade_button_switch.L2
  N2: Part1.5V, Arcade_button_switch.COM, Arcade-button_LED_(including_resistor).anode
  N3: Part1.GND, R1.Pin_1, Arcade-button_LED_(including_resistor).cathode
